# Fritzing sketch TransmitterV1 (saved by Fritzing 0.9.2b)
breadboards: 1

parts:
  Part1 = Arduino Uno (Rev3)
  Part2 = NRF24L01+ Breakout Board
  U1 = Thumb Joystick [package=joystick]

nets:
  N1: Part1.A0, U1.H
  N2: Part1.A1, U1.V
  N3: Part1.D8, Part2.CS
  N4: Part1.D11_PWM/MOSI, Part2.MOSI
  N5: Part1.D12/MISO, Part2.MISO
  N6: Part1.D13/SCK, Part2.SCK
  N7: Part1.D6_PWM, Part2.IRQ
  N8: Part1.D7, Part2.CE
  3V3: Part1.3V3, Part2.VCC
  N9: Part1.5V, U1.V+, U1.H+
  GND: Part1.GND, Part2.GND, U1.H-, U1.V-
