# Fritzing sketch TransmitterV2 (saved by Fritzing 0.9.2b)
perfboards: 1

parts:
  Part2 = NRF24L01+ Breakout Board
  U1 = Thumb Joystick [package=joystick]  # not connected
  U2 = Thumb Joystick [package=joystick]  # not connected
  U3 = M40 [package=1x40_offset]
  U4 = atmega328 [package=dip]
  C1 = Capacitor [package=cap-pth-small2]
  C2 = Capacitor [package=cap-pth-small2]
  XTAL1 = Crystal [frequency="16 Mhz" package=THT]

nets:
  N1: Part2.GND, U3.21, C1.2, C2.1
  VCC: Part2.VCC, U3.13, U4.VCC
  N2: Part2.CE, U4.D7
  N3: Part2.CS, U4.D8
  N4: Part2.SCK, U4.D13
  N5: Part2.MOSI, U4.D12
  N6: Part2.MISO, U4.D11_(PWM)
  N7: Part2.IRQ, U4.D6_(PWM)
  N8: U4.XLAT1, C2.2, XTAL1.pin_0
  N9: U4.XLAT2, C1.1, XTAL1.pin_1
