# Fritzing sketch Wiring Diagram v2 (saved by Fritzing 0.9.2b)
breadboards: 2

parts:
  Part1 = Pololu Reflectance Sensor QTR-8RC [package=qtr-8rc]
  Part3 = NRF24L01+ Breakout Board
  M1 = DC Motor
  Q1 = TRANSISTOR_NPN [package=to-92-ammo]
  Q2 = TRANSISTOR_NPN [package=to-92-ammo]
  Q3 = TRANSISTOR_NPN [package=to-92-ammo]
  Q4 = TRANSISTOR_NPN [package=to-92-ammo]
  R1 = Resistor [tolerance=±5% resistance=10k package=THT]
  R2 = Resistor [tolerance=±5% resistance=10k package=THT]
  R3 = Resistor [tolerance=±5% resistance=10k package=THT]
  R4 = Resistor [tolerance=±5% resistance=10k package=THT]
  D1 = Rectifier Diode [part_number=1N4001 package="300 mil [THT]"]
  D2 = Rectifier Diode [part_number=1N4001 package="300 mil [THT]"]
  D3 = Rectifier Diode [part_number=1N4001 package="300 mil [THT]"]
  D4 = Rectifier Diode [part_number=1N4001 package="300 mil [THT]"]
  M3 = DC Motor
  Q5 = TRANSISTOR_NPN [package=to-92-ammo]
  Q6 = TRANSISTOR_NPN [package=to-92-ammo]
  Q7 = TRANSISTOR_NPN [package=to-92-ammo]
  Q8 = TRANSISTOR_NPN [package=to-92-ammo]
  R5 = Resistor [tolerance=±5% resistance=10k package=THT]
  R6 = Resistor [tolerance=±5% resistance=10k package=THT]
  R7 = Resistor [tolerance=±5% resistance=10k package=THT]
  R8 = Resistor [tolerance=±5% resistance=10k package=THT]
  D5 = Rectifier Diode [part_number=1N4001 package="300 mil [THT]"]
  D6 = Rectifier Diode [part_number=1N4001 package="300 mil [THT]"]
  D7 = Rectifier Diode [part_number=1N4001 package="300 mil [THT]"]
  D8 = Rectifier Diode [part_number=1N4001 package="300 mil [THT]"]
  U1 = atmega328 [package=dip]
  Y1 = CRYSTAL [package=crystal-smd-5x3]
  C2 = Capacitor [package=cap-pth-small2]
  C1 = Capacitor [package=cap-pth-small2]

nets:
  N1: Part1.8, U1.D8
  N2: Part1.7, U1.D4
  N3: Part1.6, U1.A5
  N4: Part1.5, U1.A4
  N5: Part1.4, U1.A3
  N6: Part1.3, U1.A2
  N7: Part1.2, U1.A1
  N8: Part1.1, U1.A0
  N9: Part1.LEDON, U1.D2
  VCC: Part1.Vcc, Part3.VCC, Q2.C, Q3.C, D2.cathode, D3.cathode, Q6.C, Q7.C, D6.cathode, D8.cathode
  GND: Part1.GND, Part3.GND, Q1.E, Q4.E, D1.anode, D4.anode, Q5.E, Q8.E, D5.anode, D7.anode, U1.GND, C2.1, C1.2
  N10: Part3.CE, U1.D6_(PWM)
  N11: Part3.CS, U1.D7
  N12: Part3.SCK, U1.D13
  N13: Part3.MOSI, U1.D11_(PWM)
  N14: Part3.MISO, U1.D12
  N15: M1.pin_1, Q2.E, Q4.C, D2.anode, D4.cathode
  N16: M1.pin_2, Q1.C, Q3.E, D1.cathode, D3.anode
  N17: Q1.B, R2.Pin_0
  N18: Q2.B, R3.Pin_0
  N19: Q3.B, R1.Pin_0
  N20: Q4.B, R4.Pin_0
  N21: R1.Pin_1, R4.Pin_1, U1.D9_(PWM)
  N22: R2.Pin_1, R3.Pin_1, U1.D10_(PWM)
  N23: M3.pin_1, Q6.E, Q8.C, D7.cathode, D8.anode
  N24: M3.pin_2, Q5.C, Q7.E, D5.cathode, D6.anode
  N25: Q5.B, R6.Pin_0
  N26: Q6.B, R7.Pin_0
  N27: Q7.B, R5.Pin_0
  N28: Q8.B, R8.Pin_0
  N29: R5.Pin_1, R8.Pin_1, U1.D3_(PWM)
  N30: R6.Pin_1, R7.Pin_1, U1.D5_(PWM)
  N31: U1.XLAT1, Y1.2, C1.1
  N32: U1.XLAT2, Y1.1, C2.2

// code stored in the sketch: PID_V2.ino
#define DEBUG true
#define LINE_FOLLOW_STEP_INTERVAL 10 //Run line following loop every 10 milliseconds

void setup()
{
#if DEBUG
  Serial.begin(9600);
#endif

  lineFollowSetup();
}

//The last time in milliseconds from boot that the line following loop ran
long lastLineFollowStep = -1;
bool lineFollowEnabled = true;
void loop() {
  long mils = millis();

  if (lineFollowEnabled) {
    //Run the loop once every 10 milliseconds
    if ((mils - lastLineFollowStep) >= LINE_FOLLOW_STEP_INTERVAL) {

      //Run the loop
      lineFollowStep();

      //Store the time that the loop ran
      lastLineFollowStep = mils;
    }
  } else {
    halDrive(0, 0);
    halDrive(1, 0);
  }

#if DEBUG
  if (Serial.available()) {
    Serial.read();
    lineFollowEnabled = !lineFollowEnabled;
  }
#endif
}
